# Fritzing sketch ColorGlove (saved by Fritzing 0.9.2b)
breadboards: 1

parts:
  Part1 = Arduino Uno (Rev3)
  MOTOR1 = Adafruit Gear-Reduced Stepper Motor (small)  # not connected
  R1 = Slide Potentiometer [maximum_resistance=100kΩ]
  M1 = DC Motor  # not connected
  VCC1 = Battery block 9V  # not connected
  IC2 = L293D [package=THT]  # not connected
  LED1 = RGB LED (com. cathode, rbg) [package="5 mm [THT]"]
  R2 = Resistor [tolerance=±5% resistance=330 package=THT]
  Q1 = PNP-Transistor [package="SOT-23 [SMD]"]
  Q2 = PNP-Transistor [package="SOT-23 [SMD]"]
  Q3 = PNP-Transistor [package="SOT-23 [SMD]"]
  R3 = Resistor [tolerance=±5% resistance=330 package=THT]
  R4 = Resistor [tolerance=±5% resistance=330 package=THT]
  S1 = Round Pushbutton
  IC3 = L293D [package=THT]  # not connected

nets:
  N1: Part1.A0, R1.wiper
  N2: Part1.D8, S1.leg0
  N3: Part1.D9_PWM, Q1.0
  N4: Part1.D10_PWM/SS, Q3.0
  N5: Part1.D11_PWM/MOSI, Q2.0
  N6: Part1.5V, R1.leg2
  N7: Part1.GND, R1.leg1, S1.leg1
  N8: LED1.red_anode, R2.Pin_1
  N9: LED1.blue_anode, Q3.1, R3.Pin_0
  N10: LED1.green_anode, Q2.1, R4.Pin_0
  N11: R2.Pin_0, Q1.1
  N12: Q1.2, Q2.2, Q3.2

custom parts:
  Adafruit Gear-Reduced Stepper Motor (small): Adafruit gear-reduction stepper motor (small)
