# Fritzing sketch LEDBoard (saved by Fritzing 0.9.2b)
stripboards: 1

parts:
  J1 = female pin header, 2 pins [form="♀ (female)"]
  Q1 = PNP-Transistor [package="TO92 [THT]"]
  Q2 = NPN-Transistor [package="TO92 [THT]"]
  R2 = Resistor [tolerance=±5% resistance=100k package=THT]
  J2 = female pin header, 4 pins [form="♀ (female)"]
  LED1 = RGB LED (com. cathode, rgb) [package="5 mm [THT]"]
  Q3 = NPN-Transistor [package="TO92 [THT]"]
  Q4 = NPN-Transistor [package="TO92 [THT]"]
  R4 = Resistor [tolerance=±5% resistance=100k package=THT]
  R5 = Resistor [tolerance=±5% resistance=100k package=THT]
  R6 = Resistor [tolerance=±5% resistance=10k package=THT]
  R7 = Resistor [tolerance=±5% resistance=10k package=THT]
  Q5 = PNP-Transistor [package="TO92 [THT]"]
  Q6 = PNP-Transistor [package="TO92 [THT]"]
  J3 = female pin header, 2 pins [form="♀ (female)"]
  J5 = female pin header, 2 pins [form="♀ (female)"]
  IC1 = Voltage Regulator [package=to-220-alt]
  R8 = Resistor [tolerance=±5% resistance=10k package=THT]
  J7 = female pin header, 4 pins [form="♀ (female)"]
  R9 = Resistor [tolerance=±5% resistance=330 package=THT]
  VCC1 = Battery block 9V

nets:
  N1: J1.pin1, Q1.E, Q5.E, Q6.E, J3.pin1, J5.pin1, IC1.OUT
  N2: J1.pin2, Q2.E, Q3.E, Q4.E, J3.pin2, J5.pin2, J7.pin1, R9.Pin_0
  N3: Q1.B, R8.Pin_0
  N4: Q1.C, LED1.red_anode, J7.pin2
  N5: Q2.B, R2.Pin_0
  N6: Q2.C, R8.Pin_1
  N7: R2.Pin_1, J2.pin2
  N8: J2.pin3, R4.Pin_1
  N9: J2.pin4, R5.Pin_1
  N10: LED1.common_cathode, R9.Pin_1
  N11: LED1.green_anode, Q5.C, J7.pin3
  N12: LED1.blue_anode, Q6.C, J7.pin4
  N13: Q3.B, R4.Pin_0
  N14: Q3.C, R7.Pin_1
  N15: Q4.B, R5.Pin_0
  N16: Q4.C, R6.Pin_0
  N17: R6.Pin_1, Q6.B
  N18: R7.Pin_0, Q5.B
  N19: IC1.GND, VCC1.+
  N20: IC1.IN, VCC1.-
